# Fritzing sketch esphourglass (saved by Fritzing 0.9.4)
breadboards: 1

parts:
  NEOPIXEL1 = Neopixel Strip -- Black (60/m) [part_number=1461]  # not connected
  WeMos_D1_Mini1 = WeMos D1 Mini  # not connected
  S1 = Pushbutton [package="[THT]"]

nets:
  N1: S1.Pin_1, S1.Pin_2
  N2: S1.Pin_3, S1.Pin_4

custom parts:
  Neopixel Strip -- Black (60/m): Neopixel Strip, Black, 60 pixels per meter.
